# Fritzing sketch Full Diagram (saved by Fritzing 0.9.3b)

parts:
  M1 = DC Motor
  Raspberry_Pi_1 = Raspberry Pi 3 [part_number=RPI-3-V1.2]
  U1 = L298 [package=multiwatt15]
  D2F1 = D2F-FL Omron Snap Action Limit Switch with Level
  R2 = Resistor [tolerance=±5% resistance=1k package=THT]
  VCC6 = Battery block 9V

nets:
  N1: M1.pin_1, U1.CSB
  N2: M1.pin_2, U1.OUT1
  N3: Raspberry_Pi_1.GIPO17, U1.OUT2
  N4: Raspberry_Pi_1.GIPO27, U1.VS
  N5: Raspberry_Pi_1.3V3, R2.Pin_1
  N6: Raspberry_Pi_1.GIPO10, D2F1.NO, R2.Pin_0
  N7: Raspberry_Pi_1.GND, U1.CSA, U1.IN4, D2F1.COM, VCC6.-
  N8: Raspberry_Pi_1.GIPO18, U1.OUT3
  N9: Raspberry_Pi_1.5V, U1.IN1
  N10: U1.OUT4, VCC6.+

custom parts:
  D2F-FL Omron Snap Action Limit Switch with Level: Snap action switch with stainless steel lever.
