# Fritzing sketch L298N (Full Module) Diagram (saved by Fritzing 0.9.3b)

parts:
  M1 = DC Motor
  L298N1 = L298N DC motor driver
  VCC1 = Battery
  VCC2 = Battery
  VCC3 = Battery
  VCC4 = Battery
  VCC5 = Battery
  Raspberry_Pi_1 = Raspberry Pi 3 [part_number=RPI-3-V1.2]

nets:
  N1: M1.pin_1, L298N1.OUT4
  N2: M1.pin_2, L298N1.OUT3
  N3: L298N1.12V, VCC3.+
  GND: L298N1.GND, VCC5.-, Raspberry_Pi_1.GND
  5V: L298N1.5V, Raspberry_Pi_1.5V
  N4: L298N1.ENB, Raspberry_Pi_1.GIPO18
  N5: L298N1.IN3, Raspberry_Pi_1.GIPO17
  N6: L298N1.IN4, Raspberry_Pi_1.GIPO27
  N7: VCC1.-, VCC4.+
  N8: VCC1.+, VCC2.-
  N9: VCC2.+, VCC3.-
  N10: VCC4.-, VCC5.+

custom parts:
  L298N DC motor driver: 2x DC motor driver with 78M05 positive voltage regulator (7..35 V) L298N: max 46 V, 2 A Set 5 V Enable jumper to enable 5 V regultor (needed for the L298N) and +5 V output at screw terminal or supply external +5 V at screw terminal Set ENA and/or ENB to +5 V to enable motor permanently or supply ENA and/or ENB with PWM signal IN1 and IN2 set rotation directory for motor A (OUT1/OUT2) IN2 and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
