# Fritzing sketch L298N (Only IC) Diagram (saved by Fritzing 0.9.3b)

parts:
  M1 = DC Motor
  VCC1 = Battery
  VCC2 = Battery
  VCC3 = Battery
  VCC4 = Battery
  VCC5 = Battery
  Raspberry_Pi_1 = Raspberry Pi 3 [part_number=RPI-3-V1.2]
  U1 = L298 [package=multiwatt15]

nets:
  N1: M1.pin_1, U1.CSB
  N2: M1.pin_2, U1.OUT1
  N3: VCC1.-, VCC4.+
  N4: VCC1.+, VCC2.-
  N5: VCC2.+, VCC3.-
  N6: VCC3.+, U1.OUT4
  N7: VCC4.-, VCC5.+
  N8: VCC5.-, Raspberry_Pi_1.GND, U1.CSA, U1.IN4
  N9: Raspberry_Pi_1.GIPO17, U1.OUT2
  N10: Raspberry_Pi_1.GIPO27, U1.VS
  N11: Raspberry_Pi_1.GIPO18, U1.OUT3
  N12: Raspberry_Pi_1.5V, U1.IN1
